# Fritzing sketch Iluminacion-automatica (saved by Fritzing 0.9.3b)
breadboards: 1

parts:
  U2 = NodeMCU V1.0
  2_Channel_Relay1 = 2 Channel Power Relay
  Part1 = KY-018 Photoresistor Module [package="Breakout board"]

nets:
  N1: U2.D4, 2_Channel_Relay1.IN2
  3V3: U2.3V3, 2_Channel_Relay1.VCC
  GND: U2.GND, 2_Channel_Relay1.GND, Part1.-
  VIN: U2.Vin, Part1.Vin
  N2: U2.A0, Part1.S

notes:
  3.3V

custom parts:
  NodeMCU V1.0: ESP8266 based NodeMCU
  2 Channel Power Relay: A 2 channel power relay. The module operates at 5V.
  KY-018 Photoresistor Module: KY-018 Photoresistor module, used to measure light intensity. It can determine the presence or absence of light.
