# Fritzing sketch LCD (saved by Fritzing 0.9.3b)
breadboards: 1

parts:
  Componente2 = LCD1602-I2C
  U2 = NodeMCU V1.0

nets:
  GND: Componente2.GND, U2.GND
  VCC: Componente2.VCC, U2.Vin
  N1: Componente2.SDA, U2.D2
  N2: Componente2.SCL, U2.D1

notes:
  5V

custom parts:
  LCD1602-I2C: A standard character display, usually with 2x16 characters. Comes in many colors with LCM1602 IIC attached.
  NodeMCU V1.0: ESP8266 based NodeMCU
