# Fritzing sketch LCD_BME280 (saved by Fritzing 0.9.3b)
breadboards: 1

parts:
  Componente2 = LCD1602-I2C
  U2 = NodeMCU V1.0
  BMP280_Breakout1 = BMP280 Breakout Board [part_number=BMP280]

nets:
  GND: Componente2.GND, U2.GND, BMP280_Breakout1.GND
  VCC: Componente2.VCC, U2.Vin, BMP280_Breakout1.VCC
  N1: Componente2.SDA, U2.D2, BMP280_Breakout1.SDA
  N2: Componente2.SCL, U2.D1, BMP280_Breakout1.SCL

notes:
  5V
  I2C
  SCL y SDA
  I2C
  D1 - SCL
  D2 - SDA

custom parts:
  LCD1602-I2C: A standard character display, usually with 2x16 characters. Comes in many colors with LCM1602 IIC attached.
  NodeMCU V1.0: ESP8266 based NodeMCU
  BMP280 Breakout Board: This is a breakout board for the Bosch Sensortec BMP280, "an absolute barometric pressure sensor especially designed for mobile applications." The operation range is 300 to 1100 hPa. Supply voltage is 1.2 to 3.6V. Operating temperature range is -40 to +85 °C.
