# Fritzing sketch LCD_DHT (saved by Fritzing 0.9.3b)
breadboards: 1

parts:
  Componente2 = LCD1602-I2C
  U2 = NodeMCU V1.0
  Part3 = DHT22 Breakout module [package="Breakout board"]

nets:
  GND: Componente2.GND, U2.GND, Part3.-
  VCC: Componente2.VCC, U2.Vin, Part3.+
  N1: Componente2.SDA, U2.D2
  N2: Componente2.SCL, U2.D1
  N3: U2.D6, Part3.Out

notes:
  5V

custom parts:
  LCD1602-I2C: A standard character display, usually with 2x16 characters. Comes in many colors with LCM1602 IIC attached.
  NodeMCU V1.0: ESP8266 based NodeMCU
  DHT22 Breakout module: DHT22 temperature and humidity sensor module, provides a low-latency serial interface to measure humidity and temperature.
