# Fritzing sketch LCD_DHT_Humedad_Rele (saved by Fritzing 0.9.3b)
breadboards: 1

parts:
  Componente2 = LCD1602-I2C
  U2 = NodeMCU V1.0
  Part3 = DHT22 Breakout module [package="Breakout board"]
  YL-83_-_Control_Board1 = YL-83 Rain Sensor - Control Board
  Componente3 = FC-28 Soil Hygrometer Module - Probe
  2_Channel_Relay1 = 2 Channel Power Relay

nets:
  GND: Componente2.GND, U2.GND, Part3.-, YL-83_-_Control_Board1.GND, 2_Channel_Relay1.GND
  VCC: Componente2.VCC, U2.Vin, Part3.+
  N1: Componente2.SDA, U2.D2
  N2: Componente2.SCL, U2.D1
  N3: U2.D4, 2_Channel_Relay1.IN1
  VCC_2: U2.3V3, YL-83_-_Control_Board1.VCC, 2_Channel_Relay1.VCC
  N4: U2.D6, Part3.Out
  N5: U2.A0, YL-83_-_Control_Board1.AO
  N6: YL-83_-_Control_Board1.POS, Componente3.POS
  N7: YL-83_-_Control_Board1.NEG, Componente3.NEG

notes:
  5V
  3.3V

custom parts:
  LCD1602-I2C: A standard character display, usually with 2x16 characters. Comes in many colors with LCM1602 IIC attached.
  NodeMCU V1.0: ESP8266 based NodeMCU
  DHT22 Breakout module: DHT22 temperature and humidity sensor module, provides a low-latency serial interface to measure humidity and temperature.
  YL-83 Rain Sensor - Control Board: The YL-83 is a rain sensor that has more resistance when dry and less resistance when wet. The module runs at 5V.
  FC-28 Soil Hygrometer Module - Probe: The FC-28 is a soil hygrometer module that uses the Texas Instruments LM393 comparator chip to provide an analog measurement of soil humidity.
  2 Channel Power Relay: A 2 channel power relay. The module operates at 5V.
