# Fritzing sketch LED_PWM (saved by Fritzing 0.9.3b)
breadboards: 1

parts:
  U2 = NodeMCU
  R1 = Resistor [tolerance=±5% resistance=220 package=THT]
  LED1 = LED - 5mm [color="Red (633nm)" package="5 mm [THT]"]  # not connected

nets:
  N1: U2.connector8, R1.Pin_0
