# Fritzing sketch Led_Pulsador (saved by Fritzing 0.9.3b)
breadboards: 1

parts:
  9_Voltios = 2.1mm Barrel Jack with Terminal Block
  R1 = Resistor [tolerance=±5% resistance=100 package=THT]
  LED1 = LED - 5mm [color="Red (633nm)" package="5 mm [THT]"]
  LED2 = LED - 5mm [color="Red (633nm)" package="5 mm [THT]"]
  LED3 = LED - 5mm [color="Red (633nm)" package="5 mm [THT]"]
  Pulsador = Pushbutton [package="[THT]"]

nets:
  N1: 9_Voltios.POS, R1.Pin_0
  N2: 9_Voltios.NEG, LED3.cathode
  N3: R1.Pin_1, Pulsador.Pin_3, Pulsador.Pin_4
  N4: LED1.cathode, LED2.anode
  N5: LED1.anode, Pulsador.Pin_1, Pulsador.Pin_2
  N6: LED2.cathode, LED3.anode

notes:
  9V
  100 Ohmios
