# Fritzing sketch Reles (saved by Fritzing 0.9.3b)
breadboards: 1

parts:
  U2 = NodeMCU V1.0
  2_Channel_Relay1 = 2 Channel Power Relay
  JACK1 = 2.1mm Barrel Jack with Terminal Block

nets:
  N1: U2.D1, 2_Channel_Relay1.IN1
  N2: U2.D2, 2_Channel_Relay1.IN2
  GND: U2.GND, 2_Channel_Relay1.GND, JACK1.NEG
  VIN: U2.Vin, 2_Channel_Relay1.VCC, JACK1.POS

notes:
  5V

custom parts:
  NodeMCU V1.0: ESP8266 based NodeMCU
  2 Channel Power Relay: A 2 channel power relay. The module operates at 5V.
