# Fritzing sketch Reles_Carga (saved by Fritzing 0.9.3b)
breadboards: 1

parts:
  U2 = NodeMCU V1.0
  2_Channel_Relay1 = 2 Channel Power Relay
  JACK1 = 2.1mm Barrel Jack with Terminal Block
  R1 = Resistor [tolerance=±5% resistance=100 package=THT]
  LED1 = LED - 5mm [color="Red (633nm)" package="5 mm [THT]"]
  LED2 = LED - 5mm [color="Red (633nm)" package="5 mm [THT]"]
  LED3 = LED - 5mm [color="Red (633nm)" package="5 mm [THT]"]

nets:
  N1: U2.D1, 2_Channel_Relay1.IN1
  N2: U2.D2, 2_Channel_Relay1.IN2
  GND: U2.GND, 2_Channel_Relay1.GND, 2_Channel_Relay1.K1-NO, JACK1.NEG
  VIN: U2.Vin, 2_Channel_Relay1.VCC, JACK1.POS, R1.Pin_0
  N3: 2_Channel_Relay1.K1-COM, LED3.cathode
  N4: R1.Pin_1, LED1.anode
  N5: LED1.cathode, LED2.anode
  N6: LED2.cathode, LED3.anode

notes:
  9V

custom parts:
  NodeMCU V1.0: ESP8266 based NodeMCU
  2 Channel Power Relay: A 2 channel power relay. The module operates at 5V.
