# Fritzing sketch Reloj_RTC (saved by Fritzing 0.9.3b)
breadboards: 1

parts:
  Componente2 = LCD1602-I2C
  U2 = NodeMCU V1.0
  ZS-042_RTC1 = ZS-042 RTC Module

nets:
  GND: Componente2.GND, U2.GND, ZS-042_RTC1.GND
  VCC: Componente2.VCC, U2.Vin, ZS-042_RTC1.VCC
  N1: Componente2.SDA, U2.D2, ZS-042_RTC1.SDA
  N2: Componente2.SCL, U2.D1, ZS-042_RTC1.SCL

notes:
  5V

custom parts:
  LCD1602-I2C: A standard character display, usually with 2x16 characters. Comes in many colors with LCM1602 IIC attached.
  NodeMCU V1.0: ESP8266 based NodeMCU
