# Fritzing sketch alarma-Reles (saved by Fritzing 0.9.3b)
breadboards: 1

parts:
  U2 = NodeMCU V1.0
  2_Channel_Relay1 = 2 Channel Power Relay
  PIR2 = PIR sensor

nets:
  N1: U2.D2, PIR2.SIG
  N2: U2.D4, 2_Channel_Relay1.IN2
  3V3: U2.3V3, 2_Channel_Relay1.VCC
  GND: U2.GND, 2_Channel_Relay1.GND, PIR2.GND
  VIN: U2.Vin, PIR2.VDD

notes:
  3.3V

custom parts:
  NodeMCU V1.0: ESP8266 based NodeMCU
  2 Channel Power Relay: A 2 channel power relay. The module operates at 5V.
