# Fritzing sketch riego-automatica (saved by Fritzing 0.9.3b)
breadboards: 1

parts:
  U2 = NodeMCU V1.0
  2_Channel_Relay1 = 2 Channel Power Relay
  Componente1 = FC-28 Soil Hygrometer Module - Probe
  Componente2 = FC-28 Soil Hygrometer Module

nets:
  N1: U2.D4, 2_Channel_Relay1.IN2
  3V3: U2.3V3, 2_Channel_Relay1.VCC
  GND: U2.GND, 2_Channel_Relay1.GND, Componente2.GND
  VIN: U2.Vin, Componente2.VCC
  N2: U2.A0, Componente2.AO
  N3: Componente1.POS, Componente2.POS
  N4: Componente1.NEG, Componente2.NEG

notes:
  3.3V

custom parts:
  NodeMCU V1.0: ESP8266 based NodeMCU
  2 Channel Power Relay: A 2 channel power relay. The module operates at 5V.
  FC-28 Soil Hygrometer Module - Probe: The FC-28 is a soil hygrometer module that uses the Texas Instruments LM393 comparator chip to provide an analog measurement of soil humidity.
  FC-28 Soil Hygrometer Module: The FC-28 is a soil hygrometer module that uses the Texas Instruments LM393 comparator chip to provide an analog measurement of soil humidity. The digital output is high when soil moisture is over a certain threshold, as determined by adjusting the potentiometer.
